# Fritzing sketch Schaltplan (saved by Fritzing 0.9.3b)
breadboards: 1

parts:
  ESP32 = ESP32S-HiLetgo [part_number=Lolin]
  Barometer = Adafruit BME280

nets:
  N1: ESP32.3.3, Barometer.3.3V
  GND: ESP32.GND, Barometer.GND
  N2: ESP32.GPIO21, Barometer.SDI/SDA
  N3: ESP32.GPIO22, Barometer.SCK/SCL

custom parts:
  ESP32S-HiLetgo: HiLetgo ESP-WROOM-32 ESP32 ESP-32S Development Board 2.4GHz Dual-Mode WiFi + Bluetooth Dual Cores Microcontroller The ESP32 integrated with Antenna switches, RF Balun, power amplifiers, low-noise amplifiers, filters, and management modules, and the entire solution occupies the least area of PCB. 2.4 GHz Wi-Fi plus Bluetooth dual-mode chip, with TSMC Ultra-low power consumption 40nm technology,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
  Adafruit BME280: Bosch has stepped up their game with their new BME280 sensor, an environmental sensor with temperature, barometric pressure and humidity! This sensor is great for all sorts of weather/environmental sensing and can even be used in both I2C and SPI! This precision sensor from Bosch is the best low-cost sensing solution for measuring humidity with ±3% accuracy, barometric pressure with ±1 hPa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
